# Fritzing sketch wiring schematic (saved by Fritzing 1.0.2b)

parts:
  J1 = STM32 Nucleo boards
  5V = ST VL53L8CX breakout
  J2 = STM32 Nucleo boards  # not connected
  Part1 = Arduino Uno (Rev3)  # not connected
  A1 = ST VL53L8CX breakout  # not connected
  Part2 = Adafruit AS7262 Visible Spetral Sensor [part_number="Adafruit #3779"]  # not connected

nets:
  N1: J1.A2, 5V.Pin_15
  N2: J1.A3, 5V.Pin_17
  N3: J1.D11_PWM/MOSI, 5V.Pin_22
  N4: J1.A4/SDA, 5V.Pin_20
  N5: J1.A5/SCL, 5V.Pin_21
  N6: J1.5V, 5V.Pin_26
  N7: J1.GND, 5V.Pin_16
  N8: 5V.Pin_27, 5V.Pin_28

custom parts:
  ST VL53L8CX breakout: Breakout board based on the VL53L8 series Time-of-Flight sensors.
